# Fritzing sketch Zombie Cannon - Target Sites (saved by Fritzing 0.7.0b)
breadboards: 1
perfboards: 1

parts:
  LED1 = LED - 3mm [color="Green (565nm)" package="3 mm [THT]"]
  LED2 = LED - 3mm [color="Green (565nm)" package="3 mm [THT]"]
  LED3 = LED - 3mm [color="Green (565nm)" package="3 mm [THT]"]
  LED4 = LED - 3mm [color="Green (565nm)" package="3 mm [THT]"]
  LED5 = LED - 3mm [color="Green (565nm)" package="3 mm [THT]"]
  LED6 = LED - 3mm [color="Green (565nm)" package="3 mm [THT]"]
  LED7 = LED - 3mm [color="Green (565nm)" package="3 mm [THT]"]
  LED8 = LED - 3mm [color="Green (565nm)" package="3 mm [THT]"]
  LED9 = LED - 3mm [color="Green (565nm)" package="3 mm [THT]"]
  LED10 = LED - 3mm [color="Green (565nm)" package="3 mm [THT]"]
  LED11 = LED - 3mm [color="Green (565nm)" package="3 mm [THT]"]
  LED12 = LED - 3mm [color="Green (565nm)" package="3 mm [THT]"]
  LED13 = LED - 3mm [color="Green (565nm)" package="3 mm [THT]"]
  LED14 = LED - 3mm [color="Green (565nm)" package="3 mm [THT]"]
  LED15 = LED - 3mm [color="Green (565nm)" package="3 mm [THT]"]
  LED16 = LED - 3mm [color="Green (565nm)" package="3 mm [THT]"]
  LED17 = LED - 3mm [color="Yellow (574nm)" package="3 mm [THT]"]
  LED18 = LED - 3mm [color="Yellow (574nm)" package="3 mm [THT]"]
  LED19 = LED - 3mm [color="Yellow (574nm)" package="3 mm [THT]"]
  LED20 = LED - 3mm [color="Yellow (574nm)" package="3 mm [THT]"]
  LED21 = LED - 3mm [color="Yellow (574nm)" package="3 mm [THT]"]
  LED22 = LED - 3mm [color="Yellow (574nm)" package="3 mm [THT]"]
  LED23 = LED - 3mm [color="Yellow (574nm)" package="3 mm [THT]"]
  LED24 = LED - 3mm [color="Yellow (574nm)" package="3 mm [THT]"]
  LED25 = LED - 3mm [color="Red (633nm)" package="3 mm [THT]"]
  LED26 = LED - 3mm [color="Red (633nm)" package="3 mm [THT]"]
  LED27 = LED - 3mm [color="Red (633nm)" package="3 mm [THT]"]
  LED28 = LED - 3mm [color="Red (633nm)" package="3 mm [THT]"]
  LED29 = LED - 3mm [color="Red (633nm)" package="3 mm [THT]"]
  R1 = Resistor [tolerance=±5% resistance=56 package="0603 [SMD]"]
  R2 = Resistor [tolerance=±5% resistance=56 package="0603 [SMD]"]
  R3 = Resistor [tolerance=±5% resistance=56 package="0603 [SMD]"]
  R4 = Resistor [tolerance=±5% resistance=56 package="0603 [SMD]"]
  R5 = Resistor [tolerance=±5% resistance=56 package="0603 [SMD]"]
  R6 = Resistor [tolerance=±5% resistance=56 package="0603 [SMD]"]
  R7 = Resistor [tolerance=±5% resistance=56 package="0603 [SMD]"]
  R8 = Resistor [tolerance=±5% resistance=56 package="0603 [SMD]"]
  Q1 = NPN-Transistor [package="TO92 [THT]"]
  Nano1 = Arduino Nano v2.3
  R9 = Resistor [tolerance=±5% resistance=1k package="0603 [SMD]"]
  R10 = Resistor [tolerance=±5% resistance=1k package="0603 [SMD]"]
  Q2 = NPN-Transistor [package="TO92 [THT]"]
  R11 = Resistor [tolerance=±5% resistance=1k package="0603 [SMD]"]
  Q3 = NPN-Transistor [package="TO92 [THT]"]
  R12 = Resistor [tolerance=±5% resistance=1k package="0603 [SMD]"]
  Q4 = NPN-Transistor [package="TO92 [THT]"]

nets:
  N1: LED1.cathode, LED2.cathode, LED3.cathode, LED4.cathode, LED5.cathode, LED6.cathode, LED7.cathode, LED8.cathode, Q4.E
  N2: LED1.anode, LED9.anode, LED17.anode, LED28.anode, R8.Pin_0
  N3: LED2.anode, LED10.anode, LED18.anode, LED25.anode, R7.Pin_0
  N4: LED3.anode, LED11.anode, LED19.anode, LED26.anode, R6.Pin_0
  N5: LED4.anode, LED12.anode, LED20.anode, R5.Pin_0
  N6: LED5.anode, LED13.anode, LED21.anode, LED27.anode, R4.Pin_0
  N7: LED6.anode, LED14.anode, LED22.anode, R3.Pin_0
  N8: LED7.anode, LED15.anode, LED23.anode, LED29.anode, R2.Pin_0
  N9: LED8.anode, LED16.anode, LED24.anode, R1.Pin_0
  N10: LED9.cathode, LED10.cathode, LED11.cathode, LED12.cathode, LED13.cathode, LED14.cathode, LED15.cathode, LED16.cathode, Q3.E
  N11: LED17.cathode, LED18.cathode, LED19.cathode, LED20.cathode, LED21.cathode, LED22.cathode, LED23.cathode, LED24.cathode, Q2.E
  N12: LED25.cathode, LED26.cathode, LED27.cathode, LED28.cathode, LED29.cathode, Q1.E
  N13: R1.Pin_1, Nano1.D13
  N14: R2.Pin_1, Nano1.D2
  N15: R3.Pin_1, Nano1.D3
  N16: R4.Pin_1, Nano1.D4
  N17: R5.Pin_1, Nano1.D5
  N18: R6.Pin_1, Nano1.D6
  N19: R7.Pin_1, Nano1.D7
  N20: R8.Pin_1, Nano1.D8
  N21: Q1.B, R9.Pin_0
  N22: Q1.C, Nano1.GND, Q2.C, Q3.C, Q4.C
  N23: Nano1.D9, R12.Pin_1
  N24: Nano1.D10, R11.Pin_1
  N25: Nano1.D11, R10.Pin_1
  N26: Nano1.D12, R9.Pin_1
  N27: R10.Pin_0, Q2.B
  N28: R11.Pin_0, Q3.B
  N29: R12.Pin_0, Q4.B
