# Fritzing sketch Untitled Sketch 2 (saved by Fritzing 0.7.0b)
breadboards: 1

parts:
  LED1 = LED - 5mm [color="Red (633nm)" package="5 mm [THT]"]
  LED2 = LED - 5mm [color="Red (633nm)" package="5 mm [THT]"]
  LED3 = LED - 5mm [color="Red (633nm)" package="5 mm [THT]"]
  LED4 = LED - 5mm [color="Red (633nm)" package="5 mm [THT]"]
  LED5 = LED - 5mm [color="Red (633nm)" package="5 mm [THT]"]
  Q1 = NPN-Transistor [package="SOT-23 [SMD]"]
  Nano1 = Arduino Nano v2.3
  R1 = Resistor [tolerance=±5% resistance=1k package="0603 [SMD]"]
  R2 = Resistor [tolerance=±5% resistance=33 package="0603 [SMD]"]
  R3 = Resistor [tolerance=±5% resistance=33 package="0603 [SMD]"]
  R4 = Resistor [tolerance=±5% resistance=150 package="0603 [SMD]"]

nets:
  N1: LED1.cathode, R3.Pin_0
  N2: LED1.anode, LED3.cathode
  N3: LED2.cathode, R2.Pin_0
  N4: LED2.anode, LED5.cathode
  N5: LED3.anode, LED4.anode, LED5.anode, Nano1.RST
  N6: LED4.cathode, R4.Pin_0
  N7: Q1.2, Nano1.VIN
  N8: Q1.0, R1.Pin_0
  N9: Q1.1, R2.Pin_1, R3.Pin_1, R4.Pin_1
  N10: Nano1.D2, R1.Pin_1
