# Fritzing sketch Zombie Cannon - Controller Schematic (saved by Fritzing 0.7.0b)
breadboards: 1

parts:
  Q1 = NPN-Transistor [package="TO92 [THT]"]
  FEZ_Panda = FEZ Panda II
  R3 = Resistor [tolerance=±5% resistance=1k package="0603 [SMD]"]
  R4 = Resistor [tolerance=±5% resistance=10k package="0603 [SMD]"]
  LED1 = LED - 3mm [color="Green (560nm)" package="3 mm [THT]"]
  D1 = Rectifier Diode [part_number=1N4001 package="300 mil [THT]"]
  R5 = Resistor [tolerance=±5% resistance=10k package="0603 [SMD]"]
  LED2 = LED - 3mm [color="Red (633nm)" package="3 mm [THT]"]
  Part1 = EasyDriver_v44 [part_number=v4.4]
  M1 = Stepper Motor - Bipolar
  12V_Source = 4 x AAA Battery Mount
  KS2E-M-DC12_DPDT_Relay1 = KS2E-M-DC12 [part_number=KS2E-M-DC12]
  Manual_Fire = Round Pushbutton
  Solenoid_Valve = Solenoid
  Target_Site_Controller = Arduino Nano v2.3
  U1 = Voltage Regulator - 5V [part_number=L7805 package="TO220 [THT]"]
  R6 = Resistor [tolerance=±5% resistance=10k package="0603 [SMD]"]
  R7 = Resistor [tolerance=±5% resistance=1 package="0603 [SMD]"]
  Laser = LED - 3mm [color="Red (633nm)" package="3 mm [THT]"]
  C2 = Ceramic Capacitor [capacitance=0.1µF voltage=16V package="1206 [SMD, multilayer]"]
  C3_0_33uF_16V = Ceramic Capacitor [package="100 mil [THT, multilayer]"]

nets:
  GND: Q1.E, FEZ_Panda.GND, R4.Pin_0, LED1.cathode, Part1.GND, 12V_Source.-, KS2E-M-DC12_DPDT_Relay1.connector2, Manual_Fire.leg0, Target_Site_Controller.GND, U1.GND, R6.Pin_1, Laser.cathode, C2.0, C3_0_33uF_16V.0
  N1: Q1.B, R3.Pin_0
  N2: Q1.C, D1.anode, KS2E-M-DC12_DPDT_Relay1.connector1, R6.Pin_0
  5V: FEZ_Panda.5V, R5.Pin_1, Target_Site_Controller.VIN, U1.output_voltage, C2.1
  N3: FEZ_Panda.Di4, Target_Site_Controller.A4
  N4: FEZ_Panda.Di5, Target_Site_Controller.A5
  N5: FEZ_Panda.Di7, R7.Pin_0
  N6: FEZ_Panda.Di8, Part1.STEP
  N7: FEZ_Panda.Di9, Part1.DIR
  N8: FEZ_Panda.Di10, Part1.MS1
  N9: FEZ_Panda.Di11, Part1.MS2
  N10: FEZ_Panda.Di12, Part1.SLEEP
  N11: FEZ_Panda.Di13, R3.Pin_1, R4.Pin_1, LED1.anode
  N12: D1.cathode, Part1.V+, 12V_Source.+, KS2E-M-DC12_DPDT_Relay1.connector0, Solenoid_Valve.pin2, U1.input_voltage, C3_0_33uF_16V.1
  N13: R5.Pin_0, LED2.anode
  N14: LED2.cathode, KS2E-M-DC12_DPDT_Relay1.connector6, Manual_Fire.leg1, Solenoid_Valve.pin1
  N15: Part1.OUT2A, M1.A
  N16: Part1.OUT2B, M1.C
  N17: Part1.OUT1A, M1.B
  N18: Part1.OUT1B, M1.D
  N19: R7.Pin_1, Laser.anode

notes:
  5V Rail
  12V Rail
  An0 to Rangefinder
  Laser
  Boarduino

custom parts:
  FEZ Panda II: FEZ Panda II is a tiny open-source board running Microsoft .NET Micro Framework.
  Ceramic Capacitor: 100 nF multilayer Ceramic Capacitor
